// Digital circuit ALU.dig as structural Verilog
module ALU (
  input  En,
  input  [3:0] Opcode,
  input  [15:0] A,
  input  [15:0] B,
  input  CLK,
  input  Carry_In,
  input  Borrow_In,
  input  [3:0] TARGET_ADDR,
  output SCU_EN,
  output LSU_EN,
  output [15:0] OUT,
  output [3:0] TARGET,
  output WE
);

  wire _16_bitdecoderwithenablepin_1_q0, _16_bitdecoderwithenablepin_1_q1, _16_bitdecoderwithenablepin_1_q2,
       _16_bitdecoderwithenablepin_1_q3, _16_bitdecoderwithenablepin_1_q4, _16_bitdecoderwithenablepin_1_q5,
       _16_bitdecoderwithenablepin_1_q6, _16_bitdecoderwithenablepin_1_q7, _16_bitdecoderwithenablepin_1_q8,
       _16_bitdecoderwithenablepin_1_q9, _16_bitdecoderwithenablepin_1_q10,
       _16_bitdecoderwithenablepin_1_q11, _16_bitdecoderwithenablepin_1_q12,
       _16_bitdecoderwithenablepin_1_q13, alu_regctrl_1_q_0, alu_regctrl_1_q_1, alu_regctrl_1_q_2,
       alu_regctrl_1_q_3, alu_regctrl_1_q_4, alu_regctrl_1_q_5, alu_regctrl_1_q_6, alu_regctrl_1_q_7,
       alu_regctrl_1_q_8, alu_regctrl_1_q_9, alu_regctrl_1_q_a, alu_regctrl_1_q_b, alu_regctrl_1_q_c,
       alu_regctrl_1_q_d, alu_regctrl_1_rst, and_1_out, BORROW, CARRY, counter_1_ovf, multiplexer_4_out,
       multiplexer_5_out, multiplexer_6_out, not_1_out, not_2_out, or_1_out, or_2_out;
  wire [0:0] SLT, SLTU;
  wire [1:0] counter_1_out, priorityencoder_1_num;
  wire [3:0] _4_bit_reg_2_q, _4_bit_reg_3_q, _4_bit_reg_4_q, _4_bit_reg_q, alu_regctrl_1_opcode_out,
       alu_regrst_2_q, multiplexer_3_out;
  wire [15:0] alu_regrst_1_q, AND, barrel_shifter_1_data_out, mul_2_mul, MUL_HIGH, MUL_LOW,
       multiplexer_2_out, NOT, OR, ROR, SAR, SHL, SHR, SUB, SUM, undriven, undriven_2, undriven_3,
       undriven_4, undriven_5, undriven_6, undriven_7, undriven_8, undriven_9, undriven_10, undriven_11,
       undriven_12, undriven_13, undriven_14, undriven_15, undriven_16, undriven_17, undriven_18,
       undriven_19, undriven_20, undriven_21, undriven_22, undriven_23, XOR;
  wire [15:4] alu_regrst_2_q_2;
  wire [31:16] mul_1_mul;

  not not_1 (not_1_out, or_1_out);
  and and_1 (and_1_out, not_1_out, En);
  _16_BitDecoderWithEnablePin _16_bitdecoderwithenablepin_1 (
    .EN(En), .Sel_4Bit(Opcode), .Q0(_16_bitdecoderwithenablepin_1_q0), .Q1(_16_bitdecoderwithenablepin_1_q1),
    .Q2(_16_bitdecoderwithenablepin_1_q2), .Q3(_16_bitdecoderwithenablepin_1_q3),
    .Q4(_16_bitdecoderwithenablepin_1_q4), .Q5(_16_bitdecoderwithenablepin_1_q5),
    .Q6(_16_bitdecoderwithenablepin_1_q6), .Q7(_16_bitdecoderwithenablepin_1_q7),
    .Q8(_16_bitdecoderwithenablepin_1_q8), .Q9(_16_bitdecoderwithenablepin_1_q9),
    .Q10(_16_bitdecoderwithenablepin_1_q10), .Q11(_16_bitdecoderwithenablepin_1_q11),
    .Q12(_16_bitdecoderwithenablepin_1_q12), .Q13(_16_bitdecoderwithenablepin_1_q13), .Q14(SCU_EN),
    .Q15(LSU_EN));
  or or_1 (or_1_out, LSU_EN, SCU_EN);
  ALU_RegCtrl alu_regctrl_1 (
    .IsEn__Decoder(and_1_out), .CLK(CLK), ._0x0(_16_bitdecoderwithenablepin_1_q0),
    ._0x1(_16_bitdecoderwithenablepin_1_q1), ._0x2(_16_bitdecoderwithenablepin_1_q2),
    ._0x3(_16_bitdecoderwithenablepin_1_q3), ._0x4(_16_bitdecoderwithenablepin_1_q4),
    ._0x5(_16_bitdecoderwithenablepin_1_q5), ._0x6(_16_bitdecoderwithenablepin_1_q6),
    ._0x7(_16_bitdecoderwithenablepin_1_q7), ._0x8(_16_bitdecoderwithenablepin_1_q8),
    ._0x9(_16_bitdecoderwithenablepin_1_q9), ._0xA(_16_bitdecoderwithenablepin_1_q10),
    ._0xB(_16_bitdecoderwithenablepin_1_q11), ._0xC(_16_bitdecoderwithenablepin_1_q12),
    ._0xD(_16_bitdecoderwithenablepin_1_q13), ._0xE(SCU_EN), ._0xF(LSU_EN), .OPCODE_IN(Opcode),
    .Q_0(alu_regctrl_1_q_0), .Q_1(alu_regctrl_1_q_1), .Q_2(alu_regctrl_1_q_2), .Q_3(alu_regctrl_1_q_3),
    .Q_4(alu_regctrl_1_q_4), .Q_5(alu_regctrl_1_q_5), .Q_6(alu_regctrl_1_q_6), .Q_7(alu_regctrl_1_q_7),
    .Q_8(alu_regctrl_1_q_8), .Q_9(alu_regctrl_1_q_9), .Q_A(alu_regctrl_1_q_a), .Q_B(alu_regctrl_1_q_b),
    .Q_C(alu_regctrl_1_q_c), .Q_D(alu_regctrl_1_q_d), .RST(alu_regctrl_1_rst),
    .OPCODE_OUT(alu_regctrl_1_opcode_out));  // open: Q_E, Q_F
  ALU_RegRST alu_regrst_1 (.D(A), .RST(alu_regctrl_1_rst), .Q(alu_regrst_1_q));
  ALU_RegRST alu_regrst_2 (.D(B), .RST(alu_regctrl_1_rst), .Q({alu_regrst_2_q_2, alu_regrst_2_q}));
  // _16_BitRegister _16_bitregister_1: pin names not known; wires that end beside it: alu_regrst_1_q, alu_regctrl_1_q_0, CLK
  // _16_BitRegister _16_bitregister_2: pin names not known; wires that end beside it: {alu_regrst_2_q_2, alu_regrst_2_q}, alu_regctrl_1_q_0, CLK
  Add #(.Bits(16)) add_1 (.a(undriven), .b(undriven_2), .c_i(Carry_In), .s(SUM), .c_o(CARRY));
  or or_2 (or_2_out, alu_regctrl_1_rst, counter_1_ovf);
  // _16_BitRegister _16_bitregister_3: pin names not known; wires that end beside it: alu_regrst_1_q, alu_regctrl_1_q_1, CLK
  // _16_BitRegister _16_bitregister_4: pin names not known; wires that end beside it: {alu_regrst_2_q_2, alu_regrst_2_q}, alu_regctrl_1_q_1, CLK
  not not_2 (not_2_out, alu_regctrl_1_rst);
  Counter #(.Bits(2)) counter_1 (.en(not_2_out), .C(CLK), .clr(or_2_out), .out(counter_1_out), .ovf(counter_1_ovf));
  Sub #(.Bits(16)) sub_1 (.a(undriven_3), .b(undriven_4), .c_i(Borrow_In), .s(SUB), .c_o(BORROW));
  D_FF #(.Bits(4)) d_ff_1 (.D(TARGET_ADDR), .C(CLK), .Q(TARGET));  // open: nQ
  and and_2 (WE, counter_1_out[0], counter_1_out[1]);
  Multiplexer #(.Selector_Bits(4), .Bits(16)) multiplexer_1 (
    .sel(alu_regctrl_1_opcode_out), .in_0(SUM), .in_1(SUB), .in_2(MUL_LOW), .in_3(MUL_HIGH), .in_4(AND),
    .in_5(XOR), .in_6(OR), .in_7(NOT), .in_8(SAR), .in_9(SHR), .in_10(SHL), .in_11({{15{1'b0}}, SLT[0]}),
    .in_12({{15{1'b0}}, SLTU[0]}), .in_13(ROR), .in_14({16{1'b0}}), .in_15({16{1'b0}}), .out(OUT));
  // _16_BitRegister _16_bitregister_5: pin names not known; wires that end beside it: alu_regrst_1_q, alu_regctrl_1_q_2, CLK
  // _16_BitRegister _16_bitregister_6: pin names not known; wires that end beside it: {alu_regrst_2_q_2, alu_regrst_2_q}, alu_regctrl_1_q_2, CLK
  Mul #(.Signed("true"), .Bits(16)) mul_1 (.a(undriven_5), .b(undriven_6), .mul({mul_1_mul, MUL_LOW}));
  // _16_BitRegister _16_bitregister_7: pin names not known; wires that end beside it: alu_regrst_1_q, alu_regctrl_1_q_3, CLK
  // _16_BitRegister _16_bitregister_8: pin names not known; wires that end beside it: {alu_regrst_2_q_2, alu_regrst_2_q}, alu_regctrl_1_q_3, CLK
  Mul #(.Signed("true"), .Bits(16)) mul_2 (.a(undriven_7), .b(undriven_8), .mul({MUL_HIGH, mul_2_mul}));
  // _16_BitRegister _16_bitregister_9: pin names not known; wires that end beside it: alu_regrst_1_q, alu_regctrl_1_q_4, CLK
  // _16_BitRegister _16_bitregister_10: pin names not known; wires that end beside it: {alu_regrst_2_q_2, alu_regrst_2_q}, alu_regctrl_1_q_4, CLK
  _16_BitAndOP _16_bitandop_1 (.A(undriven_9), .B(undriven_10), .Q(AND));
  // _16_BitRegister _16_bitregister_11: pin names not known; wires that end beside it: alu_regrst_1_q, alu_regctrl_1_q_5, CLK
  // _16_BitRegister _16_bitregister_12: pin names not known; wires that end beside it: {alu_regrst_2_q_2, alu_regrst_2_q}, alu_regctrl_1_q_5, CLK
  _16_BitXorOP _16_bitxorop_1 (.A(undriven_11), .B(undriven_12), .Q(XOR));
  // _16_BitRegister _16_bitregister_13: pin names not known; wires that end beside it: alu_regrst_1_q, alu_regctrl_1_q_6, CLK
  // _16_BitRegister _16_bitregister_14: pin names not known; wires that end beside it: {alu_regrst_2_q_2, alu_regrst_2_q}, alu_regctrl_1_q_6, CLK
  _16_BitOrOP _16_bitorop_1 (.A(undriven_13), .B(undriven_14), .Q(OR));
  // _16_BitRegister _16_bitregister_15: pin names not known; wires that end beside it: alu_regrst_1_q, alu_regctrl_1_q_7, CLK
  _16_BitNotOP _16_bitnotop_1 (.D(undriven_15), .Q(NOT));
  // _16_BitRegister _16_bitregister_16: pin names not known; wires that end beside it: alu_regrst_1_q, alu_regctrl_1_q_8, CLK
  Register #(.Bits(4)) _4_bit_reg (.D(alu_regrst_2_q), .C(CLK), .en(alu_regctrl_1_q_8), .Q(_4_bit_reg_q));
  Multiplexer #(.Selector_Bits(2), .Bits(16)) multiplexer_2 (
    .sel(priorityencoder_1_num), .in_0(undriven_16), .in_1(undriven_17), .in_2(undriven_18),
    .in_3(undriven_19), .out(multiplexer_2_out));
  Multiplexer #(.Selector_Bits(2), .Bits(4)) multiplexer_3 (
    .sel(priorityencoder_1_num), .in_0(_4_bit_reg_q), .in_1(_4_bit_reg_2_q), .in_2(_4_bit_reg_3_q),
    .in_3(_4_bit_reg_4_q), .out(multiplexer_3_out));
  Multiplexer #(.Selector_Bits(2)) multiplexer_4 (
    .sel(priorityencoder_1_num), .in_0(1'b0), .in_1(1'b0), .in_2(1'b1), .in_3(1'b0), .out(multiplexer_4_out));
  Multiplexer #(.Selector_Bits(2)) multiplexer_5 (
    .sel(priorityencoder_1_num), .in_0(1'b1), .in_1(1'b0), .in_2(1'b0), .in_3(1'b0), .out(multiplexer_5_out));
  Multiplexer #(.Selector_Bits(2)) multiplexer_6 (
    .sel(priorityencoder_1_num), .in_0(1'b0), .in_1(1'b0), .in_2(1'b0), .in_3(1'b1), .out(multiplexer_6_out));
  Barrel_Shifter barrel_shifter_1 (
    .DATA_IN(multiplexer_2_out), .SHIFT_AMT(multiplexer_3_out), .IsLeft(multiplexer_4_out),
    .ARIGHT_LOGIC(multiplexer_5_out), .IsRotate(multiplexer_6_out), .DATA_OUT(barrel_shifter_1_data_out));
  // _16_BitRegister _16_bitregister_17: pin names not known; wires that end beside it: alu_regrst_1_q, alu_regctrl_1_q_9, CLK
  Register #(.Bits(4)) _4_bit_reg_2 (.D(alu_regrst_2_q), .C(CLK), .en(alu_regctrl_1_q_9), .Q(_4_bit_reg_2_q));
  PriorityEncoder #(.Selector_Bits(2)) priorityencoder_1 (
    .in0(alu_regctrl_1_q_8), .in1(alu_regctrl_1_q_9), .in2(alu_regctrl_1_q_a), .in3(alu_regctrl_1_q_d),
    .num(priorityencoder_1_num));  // open: any
  Demultiplexer #(.Selector_Bits(2), .Bits(16)) demultiplexer_1 (
    .sel(priorityencoder_1_num), .in(barrel_shifter_1_data_out), .out_0(SAR), .out_1(SHR), .out_2(SHL),
    .out_3(ROR));
  // _16_BitRegister _16_bitregister_18: pin names not known; wires that end beside it: alu_regrst_1_q, alu_regctrl_1_q_a, CLK
  Register #(.Bits(4)) _4_bit_reg_3 (.D(alu_regrst_2_q), .C(CLK), .en(alu_regctrl_1_q_a), .Q(_4_bit_reg_3_q));
  // _16_BitRegister _16_bitregister_19: pin names not known; wires that end beside it: alu_regrst_1_q, alu_regctrl_1_q_b, CLK
  // _16_BitRegister _16_bitregister_20: pin names not known; wires that end beside it: {alu_regrst_2_q_2, alu_regrst_2_q}, alu_regctrl_1_q_b, CLK
  Comparator #(.Signed("true"), .Bits(16)) comparator_1 (
    .a(undriven_20), .b(undriven_21), .lt(SLT[0]));  // open: gt, eq
  // _16_BitRegister _16_bitregister_21: pin names not known; wires that end beside it: alu_regrst_1_q, alu_regctrl_1_q_c, CLK
  // _16_BitRegister _16_bitregister_22: pin names not known; wires that end beside it: {alu_regrst_2_q_2, alu_regrst_2_q}, alu_regctrl_1_q_c, CLK
  Comparator #(.Bits(16)) comparator_2 (.a(undriven_22), .b(undriven_23), .lt(SLTU[0]));  // open: gt, eq
  // _16_BitRegister _16_bitregister_23: pin names not known; wires that end beside it: alu_regrst_1_q, alu_regctrl_1_q_d, CLK
  Register #(.Bits(4)) _4_bit_reg_4 (.D(alu_regrst_2_q), .C(CLK), .en(alu_regctrl_1_q_d), .Q(_4_bit_reg_4_q));

  // Notes on the sheet:
  //   WE: Enable Write
endmodule
