// Digital circuit RegisterFile.dig as structural Verilog
module RegisterFile (
  input  CLK,
  input  [15:0] D,
  input  [3:0] GPREG_InSEL,
  input  [3:0] GPREG_OutSEL,
  input  [3:0] IO_WrSel,
  input  [3:0] IO_RdSel,
  input  [7:0] BRAM_ADDR,
  input  BRAM_WE,
  input  [3:0] SetMod_IO,
  input  GPIO_0x0,
  input  GPIO_0x1,
  input  GPIO_0x2,
  input  GPIO_0x3,
  input  GPIO_0x4,
  input  GPIO_0x5,
  input  GPIO_0x6,
  input  GPIO_0x7,
  input  GPIO_0x8,
  input  GPIO_0x9,
  input  GPIO_0xA,
  input  GPIO_0xB,
  input  GPIO_0xC,
  input  GPIO_0xD,
  input  GPIO_0xE,
  input  GPIO_0xF,
  output [15:0] GPREG_DataREAD,
  output GPIO_DataREAD,
  output [15:0] BRAM_DataREAD
);

  wire decoder_2_out_0, decoder_2_out_1, decoder_2_out_2, decoder_2_out_3, decoder_2_out_4, decoder_2_out_5,
       decoder_2_out_6, decoder_2_out_7, decoder_2_out_8, decoder_2_out_9, decoder_2_out_10,
       decoder_2_out_11, decoder_2_out_12, decoder_2_out_13, decoder_2_out_14, decoder_2_out_15,
       decoder_3_out_0, decoder_3_out_1, decoder_3_out_2, decoder_3_out_3, decoder_3_out_4, decoder_3_out_5,
       decoder_3_out_6, decoder_3_out_7, decoder_3_out_8, decoder_3_out_9, decoder_3_out_10,
       decoder_3_out_11, decoder_3_out_12, decoder_3_out_13, decoder_3_out_14, decoder_3_out_15, OE_0, OE_1,
       OE_2, OE_3, OE_4, OE_5, OE_6, OE_7, OE_8, OE_9, OE_10, OE_11, OE_12, OE_13, OE_14, OE_15;
  wire [3:0] gpio_cell_2_reg_rd, gpio_cell_6_reg_rd, gpio_cell_10_reg_rd, gpio_cell_14_reg_rd;
  wire [7:0] decoder_1_out_7, decoder_1_out_15;
  wire [15:0] register_1_q, register_2_q, register_3_q, register_4_q, register_9_q, register_10_q,
       register_11_q, register_12_q, register_17_q, register_18_q, register_19_q, register_20_q,
       register_25_q, register_26_q, register_27_q, register_28_q;

  Decoder #(.Selector_Bits(4)) decoder_1 (
    .sel(IO_WrSel), .out_0(decoder_1_out_7[0]), .out_1(decoder_1_out_7[1]), .out_2(decoder_1_out_7[2]),
    .out_3(decoder_1_out_7[3]), .out_4(decoder_1_out_7[4]), .out_5(decoder_1_out_7[5]),
    .out_6(decoder_1_out_7[6]), .out_7(decoder_1_out_7[7]), .out_8(decoder_1_out_15[0]),
    .out_9(decoder_1_out_15[1]), .out_10(decoder_1_out_15[2]), .out_11(decoder_1_out_15[3]),
    .out_12(decoder_1_out_15[4]), .out_13(decoder_1_out_15[5]), .out_14(decoder_1_out_15[6]),
    .out_15(decoder_1_out_15[7]));
  Decoder #(.Selector_Bits(4)) decoder_2 (
    .sel(GPREG_InSEL), .out_0(decoder_2_out_0), .out_1(decoder_2_out_1), .out_2(decoder_2_out_2),
    .out_3(decoder_2_out_3), .out_4(decoder_2_out_4), .out_5(decoder_2_out_5), .out_6(decoder_2_out_6),
    .out_7(decoder_2_out_7), .out_8(decoder_2_out_8), .out_9(decoder_2_out_9), .out_10(decoder_2_out_10),
    .out_11(decoder_2_out_11), .out_12(decoder_2_out_12), .out_13(decoder_2_out_13),
    .out_14(decoder_2_out_14), .out_15(decoder_2_out_15));
  gpio_cell gpio_cell_1 (
    .REG_WR(D[12]), .OE(OE_0), .PIN_IN(GPIO_0x0), .CLK(CLK), .WE(decoder_1_out_7[0]),
    .REG_RD(gpio_cell_2_reg_rd[0]), .PIN_OUT(GPIO_0x0));
  gpio_cell gpio_cell_2 (
    .REG_WR(D[13]), .OE(OE_1), .PIN_IN(GPIO_0x1), .CLK(CLK), .WE(decoder_1_out_7[1]),
    .REG_RD(gpio_cell_2_reg_rd[1]), .PIN_OUT(GPIO_0x1));
  gpio_cell gpio_cell_3 (
    .REG_WR(D[14]), .OE(OE_2), .PIN_IN(GPIO_0x2), .CLK(CLK), .WE(decoder_1_out_7[2]),
    .REG_RD(gpio_cell_2_reg_rd[2]), .PIN_OUT(GPIO_0x2));
  gpio_cell gpio_cell_4 (
    .REG_WR(D[15]), .OE(OE_3), .PIN_IN(GPIO_0x3), .CLK(CLK), .WE(decoder_1_out_7[3]),
    .REG_RD(gpio_cell_2_reg_rd[3]), .PIN_OUT(GPIO_0x3));
  Decoder #(.Selector_Bits(4)) decoder_3 (
    .sel(SetMod_IO), .out_0(decoder_3_out_0), .out_1(decoder_3_out_1), .out_2(decoder_3_out_2),
    .out_3(decoder_3_out_3), .out_4(decoder_3_out_4), .out_5(decoder_3_out_5), .out_6(decoder_3_out_6),
    .out_7(decoder_3_out_7), .out_8(decoder_3_out_8), .out_9(decoder_3_out_9), .out_10(decoder_3_out_10),
    .out_11(decoder_3_out_11), .out_12(decoder_3_out_12), .out_13(decoder_3_out_13),
    .out_14(decoder_3_out_14), .out_15(decoder_3_out_15));
  Register #(.Bits(16)) register_1 (.D(D), .C(CLK), .en(decoder_2_out_0), .Q(register_1_q));
  Register #(.Bits(16)) register_2 (.D(D), .C(CLK), .en(decoder_2_out_1), .Q(register_2_q));
  Register #(.Bits(16)) register_3 (.D(D), .C(CLK), .en(decoder_2_out_2), .Q(register_3_q));
  Register #(.Bits(16)) register_4 (.D(D), .C(CLK), .en(decoder_2_out_3), .Q(register_4_q));
  BlockRAMDualPort #(.AddrBits(8), .Bits(16)) blockramdualport_1 (
    .A(BRAM_ADDR), .Din(D), .str(BRAM_WE), .C(CLK), .D(BRAM_DataREAD));
  Register register_5 (.D(D[0]), .C(CLK), .en(decoder_3_out_0), .Q(OE_0));
  Register register_6 (.D(D[0]), .C(CLK), .en(decoder_3_out_1), .Q(OE_1));
  Register register_7 (.D(D[0]), .C(CLK), .en(decoder_3_out_2), .Q(OE_2));
  Register register_8 (.D(D[0]), .C(CLK), .en(decoder_3_out_3), .Q(OE_3));
  gpio_cell gpio_cell_5 (
    .REG_WR(D[8]), .OE(OE_4), .PIN_IN(GPIO_0x4), .CLK(CLK), .WE(decoder_1_out_7[4]),
    .REG_RD(gpio_cell_6_reg_rd[0]), .PIN_OUT(GPIO_0x4));
  gpio_cell gpio_cell_6 (
    .REG_WR(D[9]), .OE(OE_5), .PIN_IN(GPIO_0x5), .CLK(CLK), .WE(decoder_1_out_7[5]),
    .REG_RD(gpio_cell_6_reg_rd[1]), .PIN_OUT(GPIO_0x5));
  gpio_cell gpio_cell_7 (
    .REG_WR(D[10]), .OE(OE_6), .PIN_IN(GPIO_0x6), .CLK(CLK), .WE(decoder_1_out_7[6]),
    .REG_RD(gpio_cell_6_reg_rd[2]), .PIN_OUT(GPIO_0x6));
  gpio_cell gpio_cell_8 (
    .REG_WR(D[11]), .OE(OE_7), .PIN_IN(GPIO_0x7), .CLK(CLK), .WE(decoder_1_out_7[7]),
    .REG_RD(gpio_cell_6_reg_rd[3]), .PIN_OUT(GPIO_0x7));
  Register #(.Bits(16)) register_9 (.D(D), .C(CLK), .en(decoder_2_out_4), .Q(register_9_q));
  Register #(.Bits(16)) register_10 (.D(D), .C(CLK), .en(decoder_2_out_5), .Q(register_10_q));
  Register #(.Bits(16)) register_11 (.D(D), .C(CLK), .en(decoder_2_out_6), .Q(register_11_q));
  Register #(.Bits(16)) register_12 (.D(D), .C(CLK), .en(decoder_2_out_7), .Q(register_12_q));
  Register register_13 (.D(D[0]), .C(CLK), .en(decoder_3_out_4), .Q(OE_4));
  Register register_14 (.D(D[0]), .C(CLK), .en(decoder_3_out_5), .Q(OE_5));
  Register register_15 (.D(D[0]), .C(CLK), .en(decoder_3_out_6), .Q(OE_6));
  Register register_16 (.D(D[0]), .C(CLK), .en(decoder_3_out_7), .Q(OE_7));
  gpio_cell gpio_cell_9 (
    .REG_WR(D[4]), .OE(OE_8), .PIN_IN(GPIO_0x8), .CLK(CLK), .WE(decoder_1_out_15[0]),
    .REG_RD(gpio_cell_10_reg_rd[0]), .PIN_OUT(GPIO_0x8));
  gpio_cell gpio_cell_10 (
    .REG_WR(D[5]), .OE(OE_9), .PIN_IN(GPIO_0x9), .CLK(CLK), .WE(decoder_1_out_15[1]),
    .REG_RD(gpio_cell_10_reg_rd[1]), .PIN_OUT(GPIO_0x9));
  gpio_cell gpio_cell_11 (
    .REG_WR(D[6]), .OE(OE_10), .PIN_IN(GPIO_0xA), .CLK(CLK), .WE(decoder_1_out_15[2]),
    .REG_RD(gpio_cell_10_reg_rd[2]), .PIN_OUT(GPIO_0xA));
  gpio_cell gpio_cell_12 (
    .REG_WR(D[7]), .OE(OE_11), .PIN_IN(GPIO_0xB), .CLK(CLK), .WE(decoder_1_out_15[3]),
    .REG_RD(gpio_cell_10_reg_rd[3]), .PIN_OUT(GPIO_0xB));
  Register #(.Bits(16)) register_17 (.D(D), .C(CLK), .en(decoder_2_out_8), .Q(register_17_q));
  Register #(.Bits(16)) register_18 (.D(D), .C(CLK), .en(decoder_2_out_9), .Q(register_18_q));
  Register #(.Bits(16)) register_19 (.D(D), .C(CLK), .en(decoder_2_out_10), .Q(register_19_q));
  Register #(.Bits(16)) register_20 (.D(D), .C(CLK), .en(decoder_2_out_11), .Q(register_20_q));
  Register register_21 (.D(D[0]), .C(CLK), .en(decoder_3_out_8), .Q(OE_8));
  Register register_22 (.D(D[0]), .C(CLK), .en(decoder_3_out_9), .Q(OE_9));
  Register register_23 (.D(D[0]), .C(CLK), .en(decoder_3_out_10), .Q(OE_10));
  Register register_24 (.D(D[0]), .C(CLK), .en(decoder_3_out_11), .Q(OE_11));
  Register #(.Bits(16)) register_25 (.D(D), .C(CLK), .en(decoder_2_out_12), .Q(register_25_q));
  Register #(.Bits(16)) register_26 (.D(D), .C(CLK), .en(decoder_2_out_13), .Q(register_26_q));
  Register #(.Bits(16)) register_27 (.D(D), .C(CLK), .en(decoder_2_out_14), .Q(register_27_q));
  Register #(.Bits(16)) register_28 (.D(D), .C(CLK), .en(decoder_2_out_15), .Q(register_28_q));
  Register register_29 (.D(D[0]), .C(CLK), .en(decoder_3_out_12), .Q(OE_12));
  Register register_30 (.D(D[0]), .C(CLK), .en(decoder_3_out_13), .Q(OE_13));
  Register register_31 (.D(D[0]), .C(CLK), .en(decoder_3_out_14), .Q(OE_14));
  Register register_32 (.D(D[0]), .C(CLK), .en(decoder_3_out_15), .Q(OE_15));
  gpio_cell gpio_cell_13 (
    .REG_WR(D[0]), .OE(OE_12), .PIN_IN(GPIO_0xC), .CLK(CLK), .WE(decoder_1_out_15[4]),
    .REG_RD(gpio_cell_14_reg_rd[0]), .PIN_OUT(GPIO_0xC));
  gpio_cell gpio_cell_14 (
    .REG_WR(D[1]), .OE(OE_13), .PIN_IN(GPIO_0xD), .CLK(CLK), .WE(decoder_1_out_15[5]),
    .REG_RD(gpio_cell_14_reg_rd[1]), .PIN_OUT(GPIO_0xD));
  gpio_cell gpio_cell_15 (
    .REG_WR(D[2]), .OE(OE_14), .PIN_IN(GPIO_0xE), .CLK(CLK), .WE(decoder_1_out_15[6]),
    .REG_RD(gpio_cell_14_reg_rd[2]), .PIN_OUT(GPIO_0xE));
  gpio_cell gpio_cell_16 (
    .REG_WR(D[3]), .OE(OE_15), .PIN_IN(GPIO_0xF), .CLK(CLK), .WE(decoder_1_out_15[7]),
    .REG_RD(gpio_cell_14_reg_rd[3]), .PIN_OUT(GPIO_0xF));
  Multiplexer #(.Selector_Bits(4), .Bits(16)) multiplexer_1 (
    .sel(GPREG_OutSEL), .in_0(register_1_q), .in_1(register_2_q), .in_2(register_3_q), .in_3(register_4_q),
    .in_4(register_9_q), .in_5(register_10_q), .in_6(register_11_q), .in_7(register_12_q),
    .in_8(register_17_q), .in_9(register_18_q), .in_10(register_19_q), .in_11(register_20_q),
    .in_12(register_25_q), .in_13(register_26_q), .in_14(register_27_q), .in_15(register_28_q),
    .out(GPREG_DataREAD));
  Multiplexer #(.Selector_Bits(4)) multiplexer_2 (
    .sel(IO_RdSel), .in_0(gpio_cell_2_reg_rd[0]), .in_1(gpio_cell_2_reg_rd[1]), .in_2(gpio_cell_2_reg_rd[2]),
    .in_3(gpio_cell_2_reg_rd[3]), .in_4(gpio_cell_6_reg_rd[0]), .in_5(gpio_cell_6_reg_rd[1]),
    .in_6(gpio_cell_6_reg_rd[2]), .in_7(gpio_cell_6_reg_rd[3]), .in_8(gpio_cell_10_reg_rd[0]),
    .in_9(gpio_cell_10_reg_rd[1]), .in_10(gpio_cell_10_reg_rd[2]), .in_11(gpio_cell_10_reg_rd[3]),
    .in_12(gpio_cell_14_reg_rd[0]), .in_13(gpio_cell_14_reg_rd[1]), .in_14(gpio_cell_14_reg_rd[2]),
    .in_15(gpio_cell_14_reg_rd[3]), .out(GPIO_DataREAD));
endmodule
