// Digital circuit gpio_cell.dig as structural Verilog
module gpio_cell (
  input  REG_WR,
  input  OE,
  input  PIN_IN,
  input  CLK,
  input  WE,
  output REG_RD,
  output PIN_OUT
);

  wire register_1_q;

  Register register_1 (.D(REG_WR), .C(CLK), .en(WE), .Q(register_1_q));
  assign PIN_OUT = OE ? register_1_q : 1'bz;  // Driver driver_1

  assign REG_RD = PIN_IN;
endmodule
