// Digital circuit lsu.dig as structural Verilog
module lsu (
  input  LSU_EN,
  input  [3:0] LSU_OP,
  input  CLK,
  input  [3:0] SOURCE,
  input  [3:0] TARGET,
  input  [15:0] DATA,
  input  LSU_EN_2,
  input  [3:0] LSU_OP_2,
  input  CLK_2,
  input  [3:0] SOURCE_2,
  input  [3:0] TARGET_2,
  input  [15:0] DATA_2,
  output [3:0] SOURCE_SEL,
  output [3:0] TARGET_SEL,
  output [3:0] SOURCE_SEL_2,
  output [3:0] TARGET_SEL_2
);

  wire _16_bitdecoderwithenablepin_1_q0, _16_bitdecoderwithenablepin_1_q1, _16_bitdecoderwithenablepin_1_q2,
       _16_bitdecoderwithenablepin_1_q3, _16_bitdecoderwithenablepin_1_q4, _16_bitdecoderwithenablepin_1_q5,
       _16_bitdecoderwithenablepin_1_q6, _16_bitdecoderwithenablepin_1_q7, _16_bitdecoderwithenablepin_1_q8,
       _16_bitdecoderwithenablepin_1_q9, _16_bitdecoderwithenablepin_1_q10,
       _16_bitdecoderwithenablepin_1_q11, _16_bitdecoderwithenablepin_1_q12,
       _16_bitdecoderwithenablepin_1_q13, _16_bitdecoderwithenablepin_1_q14,
       _16_bitdecoderwithenablepin_1_q15, _16_bitdecoderwithenablepin_2_q0, _16_bitdecoderwithenablepin_2_q1,
       _16_bitdecoderwithenablepin_2_q2, _16_bitdecoderwithenablepin_2_q3, _16_bitdecoderwithenablepin_2_q4,
       _16_bitdecoderwithenablepin_2_q5, _16_bitdecoderwithenablepin_2_q6, _16_bitdecoderwithenablepin_2_q7,
       _16_bitdecoderwithenablepin_2_q8, _16_bitdecoderwithenablepin_2_q9, _16_bitdecoderwithenablepin_2_q10,
       _16_bitdecoderwithenablepin_2_q11, _16_bitdecoderwithenablepin_2_q12,
       _16_bitdecoderwithenablepin_2_q13, _16_bitdecoderwithenablepin_2_q14,
       _16_bitdecoderwithenablepin_2_q15, alu_regctrl_1_q_1, alu_regctrl_1_q_2, alu_regctrl_1_q_3,
       alu_regctrl_1_q_4, alu_regctrl_1_q_5, alu_regctrl_1_q_6, alu_regctrl_1_q_7, alu_regctrl_1_q_8,
       alu_regctrl_1_q_9, alu_regctrl_1_q_a, alu_regctrl_1_q_b, alu_regctrl_1_q_c, alu_regctrl_1_q_d,
       alu_regctrl_1_q_e, alu_regctrl_1_q_f, alu_regctrl_1_rst, alu_regctrl_2_q_1, alu_regctrl_2_q_2,
       alu_regctrl_2_q_3, alu_regctrl_2_q_4, alu_regctrl_2_q_5, alu_regctrl_2_q_6, alu_regctrl_2_q_7,
       alu_regctrl_2_q_8, alu_regctrl_2_q_9, alu_regctrl_2_q_a, alu_regctrl_2_q_b, alu_regctrl_2_q_c,
       alu_regctrl_2_q_d, alu_regctrl_2_q_e, alu_regctrl_2_q_f, alu_regctrl_2_rst, or_1_out;
  wire [15:8] undriven, undriven_2;

  Register #(.Bits(4)) register_1 (.D(SOURCE_2), .C(CLK_2), .en(LSU_EN_2), .Q(SOURCE_SEL_2));
  Register #(.Bits(4)) register_2 (.D(TARGET_2), .C(CLK_2), .en(LSU_EN_2), .Q(TARGET_SEL_2));
  _16_BitDecoderWithEnablePin _16_bitdecoderwithenablepin_1 (
    .EN(LSU_EN_2), .Sel_4Bit(LSU_OP_2), .Q0(_16_bitdecoderwithenablepin_1_q0),
    .Q1(_16_bitdecoderwithenablepin_1_q1), .Q2(_16_bitdecoderwithenablepin_1_q2),
    .Q3(_16_bitdecoderwithenablepin_1_q3), .Q4(_16_bitdecoderwithenablepin_1_q4),
    .Q5(_16_bitdecoderwithenablepin_1_q5), .Q6(_16_bitdecoderwithenablepin_1_q6),
    .Q7(_16_bitdecoderwithenablepin_1_q7), .Q8(_16_bitdecoderwithenablepin_1_q8),
    .Q9(_16_bitdecoderwithenablepin_1_q9), .Q10(_16_bitdecoderwithenablepin_1_q10),
    .Q11(_16_bitdecoderwithenablepin_1_q11), .Q12(_16_bitdecoderwithenablepin_1_q12),
    .Q13(_16_bitdecoderwithenablepin_1_q13), .Q14(_16_bitdecoderwithenablepin_1_q14),
    .Q15(_16_bitdecoderwithenablepin_1_q15));
  _16_BitDecoderWithEnablePin _16_bitdecoderwithenablepin_2 (
    .EN(LSU_EN), .Sel_4Bit(LSU_OP), .Q0(_16_bitdecoderwithenablepin_2_q0),
    .Q1(_16_bitdecoderwithenablepin_2_q1), .Q2(_16_bitdecoderwithenablepin_2_q2),
    .Q3(_16_bitdecoderwithenablepin_2_q3), .Q4(_16_bitdecoderwithenablepin_2_q4),
    .Q5(_16_bitdecoderwithenablepin_2_q5), .Q6(_16_bitdecoderwithenablepin_2_q6),
    .Q7(_16_bitdecoderwithenablepin_2_q7), .Q8(_16_bitdecoderwithenablepin_2_q8),
    .Q9(_16_bitdecoderwithenablepin_2_q9), .Q10(_16_bitdecoderwithenablepin_2_q10),
    .Q11(_16_bitdecoderwithenablepin_2_q11), .Q12(_16_bitdecoderwithenablepin_2_q12),
    .Q13(_16_bitdecoderwithenablepin_2_q13), .Q14(_16_bitdecoderwithenablepin_2_q14),
    .Q15(_16_bitdecoderwithenablepin_2_q15));
  Register #(.Bits(4)) register_3 (.D(SOURCE), .C(CLK), .en(LSU_EN), .Q(SOURCE_SEL));
  Register #(.Bits(4)) register_4 (.D(TARGET), .C(CLK), .en(LSU_EN), .Q(TARGET_SEL));
  ALU_RegCtrl alu_regctrl_1 (
    .IsEn__Decoder(LSU_EN_2), .CLK(CLK_2), ._0x0(_16_bitdecoderwithenablepin_1_q0),
    ._0x1(_16_bitdecoderwithenablepin_1_q1), ._0x2(_16_bitdecoderwithenablepin_1_q2),
    ._0x3(_16_bitdecoderwithenablepin_1_q3), ._0x4(_16_bitdecoderwithenablepin_1_q4),
    ._0x5(_16_bitdecoderwithenablepin_1_q5), ._0x6(_16_bitdecoderwithenablepin_1_q6),
    ._0x7(_16_bitdecoderwithenablepin_1_q7), ._0x8(_16_bitdecoderwithenablepin_1_q8),
    ._0x9(_16_bitdecoderwithenablepin_1_q9), ._0xA(_16_bitdecoderwithenablepin_1_q10),
    ._0xB(_16_bitdecoderwithenablepin_1_q11), ._0xC(_16_bitdecoderwithenablepin_1_q12),
    ._0xD(_16_bitdecoderwithenablepin_1_q13), ._0xE(_16_bitdecoderwithenablepin_1_q14),
    ._0xF(_16_bitdecoderwithenablepin_1_q15), .Q_1(alu_regctrl_1_q_1), .Q_2(alu_regctrl_1_q_2),
    .Q_3(alu_regctrl_1_q_3), .Q_4(alu_regctrl_1_q_4), .Q_5(alu_regctrl_1_q_5), .Q_6(alu_regctrl_1_q_6),
    .Q_7(alu_regctrl_1_q_7), .Q_8(alu_regctrl_1_q_8), .Q_9(alu_regctrl_1_q_9), .Q_A(alu_regctrl_1_q_a),
    .Q_B(alu_regctrl_1_q_b), .Q_C(alu_regctrl_1_q_c), .Q_D(alu_regctrl_1_q_d), .Q_E(alu_regctrl_1_q_e),
    .Q_F(alu_regctrl_1_q_f), .RST(alu_regctrl_1_rst));  // open: Q_0
  ALU_RegCtrl alu_regctrl_2 (
    .IsEn__Decoder(LSU_EN), .CLK(CLK), ._0x0(_16_bitdecoderwithenablepin_2_q0),
    ._0x1(_16_bitdecoderwithenablepin_2_q1), ._0x2(_16_bitdecoderwithenablepin_2_q2),
    ._0x3(_16_bitdecoderwithenablepin_2_q3), ._0x4(_16_bitdecoderwithenablepin_2_q4),
    ._0x5(_16_bitdecoderwithenablepin_2_q5), ._0x6(_16_bitdecoderwithenablepin_2_q6),
    ._0x7(_16_bitdecoderwithenablepin_2_q7), ._0x8(_16_bitdecoderwithenablepin_2_q8),
    ._0x9(_16_bitdecoderwithenablepin_2_q9), ._0xA(_16_bitdecoderwithenablepin_2_q10),
    ._0xB(_16_bitdecoderwithenablepin_2_q11), ._0xC(_16_bitdecoderwithenablepin_2_q12),
    ._0xD(_16_bitdecoderwithenablepin_2_q13), ._0xE(_16_bitdecoderwithenablepin_2_q14),
    ._0xF(_16_bitdecoderwithenablepin_2_q15), .Q_1(alu_regctrl_2_q_1), .Q_2(alu_regctrl_2_q_2),
    .Q_3(alu_regctrl_2_q_3), .Q_4(alu_regctrl_2_q_4), .Q_5(alu_regctrl_2_q_5), .Q_6(alu_regctrl_2_q_6),
    .Q_7(alu_regctrl_2_q_7), .Q_8(alu_regctrl_2_q_8), .Q_9(alu_regctrl_2_q_9), .Q_A(alu_regctrl_2_q_a),
    .Q_B(alu_regctrl_2_q_b), .Q_C(alu_regctrl_2_q_c), .Q_D(alu_regctrl_2_q_d), .Q_E(alu_regctrl_2_q_e),
    .Q_F(alu_regctrl_2_q_f), .RST(alu_regctrl_2_rst));  // open: Q_0
  Register #(.Bits(16)) register_5 (.D({undriven, DATA[7:0]}), .C(CLK), .en(alu_regctrl_2_q_1));  // open: Q
  or or_1 (or_1_out, alu_regctrl_1_q_2, alu_regctrl_1_q_4, alu_regctrl_1_q_5, alu_regctrl_1_q_6);
  Register #(.Bits(16)) register_6 (.D(DATA), .C(CLK), .en(alu_regctrl_2_q_2));  // open: Q
  Register #(.Bits(16)) register_7 (.en(or_1_out));  // open: D, C, Q
  Register #(.Bits(16)) register_8 (.D({undriven_2, DATA[7:0]}), .C(CLK), .en(alu_regctrl_2_q_3));  // open: Q
  Register #(.Bits(16)) register_9 (.D(DATA), .C(CLK), .en(alu_regctrl_2_q_4));  // open: Q
  Register register_10 (.D(DATA[0]), .C(CLK), .en(alu_regctrl_2_q_5));  // open: Q
  Register register_11 (.D(DATA[0]), .C(CLK), .en(alu_regctrl_2_q_6));  // open: Q
  Register register_12 (.D(DATA[0]), .C(CLK), .en(alu_regctrl_2_q_7));  // open: Q
  // Pins of 1 and 4 bits meet at TARGET_SEL
  // Pins of 1 and 16 bits meet at DATA
  // Pins of 1 and 4 bits meet at TARGET_SEL_2

  // Notes on the sheet:
  //   DATA: This pipeline get data from source register
  //   DATA_2: This pipeline get data from source register
  //   LDB
  //   LDW
  //   STB
  //   STW
  //   STIO
  //   LDIO
  //   MOV
endmodule
